// Logisim project Sagui_Vetorial.circ as structural Verilog
module SPE_Register_Bank (
  input  [7:0] Data,
  input  [1:0] RA,
  input  WE,
  input  [1:0] RD,
  input  [1:0] RB,
  input  Clk,
  input  R,
  output [7:0] RD1,
  output [7:0] RD2
);

  wire demultiplexer_1_out0, R1, R2, R3;
  wire [7:0] D1, D2, D3;

  // NoConnect on demultiplexer_1_out0
  Demultiplexer #(.select(2)) demultiplexer_1 (
    .out0(demultiplexer_1_out0), .out1(R1), .out2(R2), .out3(R3), .in(WE), .sel(RD));
  Register u_R1 (.D(Data), .en(R1), .clk(Clk), .Q(D1), .clr(R));
  Register u_R2 (.D(Data), .en(R2), .clk(Clk), .Q(D2), .clr(R));
  Register u_R3 (.D(Data), .en(R3), .clk(Clk), .Q(D3), .clr(R));
  Multiplexer #(.select(2), .width(8)) multiplexer_1 (
    .in0({8{1'b0}}), .in1(D1), .in2(D2), .in3(D3), .out(RD1), .sel(RA));
  Multiplexer #(.select(2), .width(8)) multiplexer_2 (
    .in0({8{1'b0}}), .in1(D1), .in2(D2), .in3(D3), .out(RD2), .sel(RB));

  // Notes on the sheet:
  //   R0
endmodule

module SPE_ULA (
  input  [7:0] in_1,
  input  [7:0] in_2,
  output [7:0] out_3
);

  Adder adder_1 ();  // open: a, b, out, cin, cout
  Subtractor subtractor_1 ();  // open: a, b, out, bin, bout
  // AND_Gate and_1 is placed but not wired
  // NoConnect on in_2[7:4]
  // NoConnect on in_1[7:4]
  // NOR_Gate nor_1 is placed but not wired

  assign out_3 = {in_1[3:0], in_2[3:0]};

  // Notes on the sheet:
  //   Move High
endmodule
