// Logisim project t3.circ as structural Verilog: 9 circuits, main circuit main
module main (
);

  wire and_1_out, and_2_out, brcomp, brzi, brzr, clk, Enmov, jr, load, mov, movhl, or_1_out, reset, store,
       wbr1, wbr2, wbrldmov;
  wire [1:0] multiplexer_3_out, multiplexer_5_out;
  wire [2:0] Ulaop1, Ulaop2;
  wire [3:0] imm4br, imm4mov;
  wire [7:0] A, A1, Abranch, adder_1_out, addr, B, B1, Bbranch, dado1, dado2, dadomem, dadomov, datamem,
       imm8br, inst3ULA, inst4ULA, multiplexer_2_out, multiplexer_4_out, PC, rom_1_p2, stinmov;
  wire [7:4] inst1LDST, inst2BRANCH;

  // ROM #(.line("quad")) rom_1: pin names not known; wires that end beside it: PC, rom_1_p2, {inst1LDST, imm4mov}, {inst2BRANCH, imm4br}, inst3ULA, inst4ULA
  Button u_reset (.out(reset));
  Multiplexer #(.width(8)) multiplexer_1 (.in0(8'h4), .in1(imm8br), .out(rom_1_p2), .sel(and_1_out));
  and and_1 (and_1_out, brzi, brcomp);
  Clock #(.highDuration(2), .lowDuration(2), .phaseOffset(1)) clock_1 (.out(clk));
  Adder adder_1 (.a(PC), .b(rom_1_p2), .out(adder_1_out));  // open: cin, cout
  and and_2 (and_2_out, brzr, brcomp);
  Multiplexer #(.width(8)) multiplexer_2 (.in0(adder_1_out), .in1(Bbranch), .out(multiplexer_2_out), .sel(or_1_out));
  or or_1 (or_1_out, and_2_out, jr);
  Register u_Pc (.D(multiplexer_2_out), .en(1'b1), .clk(clk), .Q(PC), .clr(reset));
  Multiplexer #(.width(2)) multiplexer_3 (.in0(imm4mov[1:0]), .in1(2'b00), .out(multiplexer_3_out), .sel(mov));
  Multiplexer #(.width(8)) multiplexer_4 (.in0(dadomem), .in1(dadomov), .out(multiplexer_4_out), .sel(mov));
  Multiplexer #(.width(2)) multiplexer_5 (.in0(imm4mov[1:0]), .in1(2'b00), .out(multiplexer_5_out), .sel(mov));
  compbrz compbrz_1 (.A(Abranch), .brzr(brcomp));
  extSinal8bits extsinal8bits_1 (.imm4(imm4br), .imm8(imm8br));
  BancoReg bancoreg_1 (
    .clk(clk), .reset(reset), .d1(dado1), .d2(dado2), .dmemmov(multiplexer_4_out), .w1(wbr1),
    .SelW1(inst3ULA[1:0]), .w2(wbr2), .SelW2(inst4ULA[1:0]), .wld(wbrldmov), .Selld(multiplexer_3_out),
    .SelA(inst3ULA[1:0]), .SelB(inst3ULA[3:2]), .SelA1(inst4ULA[1:0]), .SelB1(inst4ULA[3:2]),
    .Selstaddr(imm4mov[3:2]), .Selstinmv(multiplexer_5_out), .Selbranchrb(imm4br[3:2]), .Enablemov(Enmov),
    .A(A), .B(B), .A1(A1), .B1(B1), .staddr(addr), .stinmv(stinmov), .branchrb(Abranch), .branchra(Bbranch));
  movhighmovlow movhighmovlow_1 (.A(stinmov), .imm(imm4mov), .Seletor(movhl), .R(dadomov));
  lookupulaop lookupulaop_1 (.Opcode(inst3ULA[7:4]), .Ulaop(Ulaop1));
  lookupulaop lookupulaop_2 (.Opcode(inst4ULA[7:4]), .Ulaop(Ulaop2));
  ULA Ula1 (.A(A), .B(B), .Seletor(Ulaop1), .R(dado1));
  ULA Ula2 (.A(A1), .B(B1), .Seletor(Ulaop2), .R(dado2));
  RAM #(.clearpin("true")) MemDados (
    .addr(addr), .we(store), .oe(load), .clk(clk), .din(stinmov), .dout(datamem), .clr(reset));
  ROM MemControle ();  // open: addr, data

  // Other names for the same wires on the sheet: inst1LDST[3:0] = imm4mov; ra1[1:0] = imm4mov[1:0];
  //   rb1[1:0] = imm4mov[3:2]; opcode1[3:0] = inst1LDST; inst2BRANCH[3:0] = imm4br; ra2[1:0] = imm4br[1:0];
  //   rb2[1:0] = imm4br[3:2]; opcode2[3:0] = inst2BRANCH; ra3[1:0] = inst3ULA[1:0]; rb3[1:0] = inst3ULA[3:2];
  //   opcode3[3:0] = inst3ULA[7:4]; ra4[1:0] = inst4ULA[1:0]; rb4[1:0] = inst4ULA[3:2]; opcode4[3:0] = inst4ULA[7:4]

  // Notes on the sheet:
  //   brzi
  //   contents of rom_1 (hex, n*v repeats v):
  //   1 2 3 4 e f 88 99
  //   mov
  //   ld st
  //   brzi
  //   brzr e jr
  //   TODO imm8br shiftado Bbranch shiftado
  //   Quatro instrucoes formam uma instrucao longa
  //   MemInst
  //   As subinstrucoes sao direcionadas para cada unidade funcional
  //   TODO nop r0 r0 -> ajustar hardware
  //   brzr e jr
  //   TODO alterar com os sinais de controle
  //   Escrita: seleciona ra para st ou r0 para mov
  //   TODO escrita sinal de controle 0 ld e 1 mov
  //   ld mov write
  //   TODO leitura sinal de controle 0 ld e 1 mov
  //   TODO escrita sinal de controle w1 w2 e wld
  //   TODO dados sinal de controle 0 ld e 1 mov
  //   TODO como fazer nop para as outras unidades func
  //   TODO nop vai ser um or de ra com ra
  //   ula1
  //   ula2
  //   st mov read
  //   ula1
  //   ula2
  //   Leitura: seleciona ra para st ou r0 para mov
  //   TODO ver se ld e st tao funcionando
  //   TODO sinal de controle 0h e 1l
  //   Identificar se r0 == 0 em brzi ou brzr 
  //   Operacao movhigh movlow
  //   Selecionar ulaop de acordo com o opcode para ula1 e ula2
  //   ra3
  //   rb3
  //   ra4
  //   rb4
  //   rb1
  //   brzi brzr jr
  //   ra1: entrada de dados
  //   ou entrada mov
  //   TESTE Reseta a memDados se apertar reset
  //   TODO load store na memcontrole
endmodule

module BancoReg (
  input  clk,
  input  reset,
  input  [7:0] d1,
  input  [7:0] d2,
  input  [7:0] dmemmov,
  input  w1,
  input  [1:0] SelW1,
  input  w2,
  input  [1:0] SelW2,
  input  wld,
  input  [1:0] Selld,
  input  [1:0] SelA,
  input  [1:0] SelB,
  input  [1:0] SelA1,
  input  [1:0] SelB1,
  input  [1:0] Selstaddr,
  input  [1:0] Selstinmv,
  input  [1:0] Selbranchrb,
  input  Enablemov,
  output [7:0] A,
  output [7:0] B,
  output [7:0] A1,
  output [7:0] B1,
  output [7:0] staddr,
  output [7:0] stinmv,
  output [7:0] branchrb,
  output [7:0] branchra
);

  wire and_1_out, or_1_out, or_2_out, or_3_out, or_4_out, w0, w0ldmov, w1_t, w1ld, w02, w2_t, w2ld, w3, w3ld,
       w12, w22, w32;
  wire [7:0] l1, l2, l3, multiplexer_8_out, multiplexer_9_out, multiplexer_10_out, multiplexer_11_out,
       multiplexer_12_out, multiplexer_13_out, multiplexer_14_out, multiplexer_15_out;

  Demultiplexer #(.select(2)) demultiplexer_1 (.out0(w0), .out1(w1_t), .out2(w2_t), .out3(w3), .in(w1), .sel(SelW1));
  Demultiplexer #(.select(2)) demultiplexer_2 (.out0(w02), .out1(w12), .out2(w22), .out3(w32), .in(w2), .sel(SelW2));
  and and_1 (and_1_out, wld, Enablemov);
  Demultiplexer #(.select(2)) demultiplexer_3 (
    .out0(w0ldmov), .out1(w1ld), .out2(w2ld), .out3(w3ld), .in(and_1_out), .sel(Selld));
  Multiplexer #(.select(2), .width(8)) multiplexer_1 (
    .in0(branchra), .in1(l1), .in2(l2), .in3(l3), .out(A), .sel(SelA));
  Multiplexer #(.select(2), .width(8)) multiplexer_2 (
    .in0(branchra), .in1(l1), .in2(l2), .in3(l3), .out(B), .sel(SelB));
  Multiplexer #(.select(2), .width(8)) multiplexer_3 (
    .in0(branchra), .in1(l1), .in2(l2), .in3(l3), .out(A1), .sel(SelA1));
  Multiplexer #(.select(2), .width(8)) multiplexer_4 (
    .in0(branchra), .in1(l1), .in2(l2), .in3(l3), .out(B1), .sel(SelB1));
  Multiplexer #(.select(2), .width(8)) multiplexer_5 (
    .in0(branchra), .in1(l1), .in2(l2), .in3(l3), .out(staddr), .sel(Selstaddr));
  Multiplexer #(.select(2), .width(8)) multiplexer_6 (
    .in0(branchra), .in1(l1), .in2(l2), .in3(l3), .out(stinmv), .sel(Selstinmv));
  Multiplexer #(.select(2), .width(8)) multiplexer_7 (
    .in0(branchra), .in1(l1), .in2(l2), .in3(l3), .out(branchrb), .sel(Selbranchrb));
  Multiplexer #(.width(8)) multiplexer_8 (.in0(d1), .in1(d2), .out(multiplexer_8_out), .sel(w02));
  Multiplexer #(.width(8)) multiplexer_9 (.in0(d1), .in1(d2), .out(multiplexer_9_out), .sel(w12));
  Multiplexer #(.width(8)) multiplexer_10 (
    .in0(multiplexer_8_out), .in1(dmemmov), .out(multiplexer_10_out), .sel(w0ldmov));
  or or_1 (or_1_out, w0, w02, w0ldmov);
  or or_2 (or_2_out, w1_t, w12, w1ld);
  Register r0 (.D(multiplexer_10_out), .en(or_1_out), .clk(clk), .Q(branchra), .clr(reset));
  Multiplexer #(.width(8)) multiplexer_11 (
    .in0(multiplexer_9_out), .in1(dmemmov), .out(multiplexer_11_out), .sel(w1ld));
  Register r1 (.D(multiplexer_11_out), .en(or_2_out), .clk(clk), .Q(l1), .clr(reset));
  Multiplexer #(.width(8)) multiplexer_12 (.in0(d1), .in1(d2), .out(multiplexer_12_out), .sel(w22));
  Multiplexer #(.width(8)) multiplexer_13 (.in0(d1), .in1(d2), .out(multiplexer_13_out), .sel(w32));
  or or_3 (or_3_out, w3, w32, w3ld);
  Multiplexer #(.width(8)) multiplexer_14 (
    .in0(multiplexer_12_out), .in1(dmemmov), .out(multiplexer_14_out), .sel(w2ld));
  or or_4 (or_4_out, w2_t, w22, w2ld);
  Multiplexer #(.width(8)) multiplexer_15 (
    .in0(multiplexer_13_out), .in1(dmemmov), .out(multiplexer_15_out), .sel(w3ld));
  Register r3 (.D(multiplexer_15_out), .en(or_3_out), .clk(clk), .Q(l3), .clr(reset));
  Register r2 (.D(multiplexer_14_out), .en(or_4_out), .clk(clk), .Q(l2), .clr(reset));

  // Other names for the same wires on the sheet: data1[7:0] = d1; data2[7:0] = d2; datamemmov[7:0] = dmemmov;
  //   Enmov = Enablemov; l0[7:0] = branchra

  // Notes on the sheet:
  //   Escrita 1
  //   Escrita 2
  //   Escrita ld mov
  //   Leitura branch
  //   Leitura A
  //   Leitura B
  //   Leitura A1
  //   Leitura B1
  //   Leitura St mov
  //   Leitura St mov
  //   Leitura branch
endmodule

module extSinal8bits (
  input  [3:0] imm4,
  output [7:0] imm8
);


  assign imm8 = {{5{imm4[3]}}, imm4[2:0]};
endmodule

module ULA (
  input  [7:0] A,
  input  [7:0] B,
  input  [2:0] Seletor,
  output [7:0] R
);

  wire [0:0] R3;
  wire [7:0] R0, R1, R2, R4, R5, R6, R7;

  Multiplexer #(.select(3), .width(8)) multiplexer_1 (
    .in0(R0), .in1(R1), .in2(R2), .in3({{7{1'b0}}, R3[0]}), .in4(R4), .in5(R5), .in6(R6), .in7(R7), .out(R),
    .sel(Seletor));
  Adder adder_1 (.a(A), .b(B), .out(R0));  // open: cin, cout
  Subtractor subtractor_1 (.a(A), .b(B), .out(R1));  // open: bin, bout
  assign R2 = A | B;  // OR_Gate or_1, 8 bits wide
  nor nor_1 (R3[0], B[0], B[1], B[2], B[3], B[4], B[5], B[6], B[7]);
  slr slr_1 (.A(A), .B(B), .R(R4));
  srr srr_1 (.A(A), .B(B), .R(R5));

  // Notes on the sheet:
  //   Add
  //   Sub
endmodule

module slr (
  input  [7:0] A,
  input  [7:0] B,
  output [7:0] R
);

  wire multiplexer_1_out, multiplexer_2_out, multiplexer_3_out, multiplexer_4_out, multiplexer_5_out,
       multiplexer_6_out, multiplexer_7_out, multiplexer_8_out, multiplexer_9_out, multiplexer_10_out,
       multiplexer_11_out, multiplexer_12_out, multiplexer_13_out, multiplexer_14_out, multiplexer_15_out,
       multiplexer_16_out, multiplexer_17_out, multiplexer_18_out, multiplexer_19_out, multiplexer_20_out,
       multiplexer_21_out, multiplexer_22_out, multiplexer_23_out, multiplexer_24_out, or_1_out;

  Multiplexer multiplexer_1 (.in0(A[0]), .in1(1'b0), .out(multiplexer_1_out), .sel(B[0]));
  Multiplexer multiplexer_2 (.in0(A[1]), .in1(A[0]), .out(multiplexer_2_out), .sel(B[0]));
  Multiplexer multiplexer_3 (.in0(A[2]), .in1(A[1]), .out(multiplexer_3_out), .sel(B[0]));
  Multiplexer multiplexer_4 (.in0(A[3]), .in1(A[2]), .out(multiplexer_4_out), .sel(B[0]));
  Multiplexer multiplexer_5 (.in0(A[4]), .in1(A[3]), .out(multiplexer_5_out), .sel(B[0]));
  Multiplexer multiplexer_6 (.in0(A[5]), .in1(A[4]), .out(multiplexer_6_out), .sel(B[0]));
  Multiplexer multiplexer_7 (.in0(A[6]), .in1(A[5]), .out(multiplexer_7_out), .sel(B[0]));
  Multiplexer multiplexer_8 (.in0(A[7]), .in1(A[6]), .out(multiplexer_8_out), .sel(B[0]));
  Multiplexer multiplexer_9 (.in0(multiplexer_1_out), .in1(1'b0), .out(multiplexer_9_out), .sel(B[1]));
  Multiplexer multiplexer_10 (.in0(multiplexer_2_out), .in1(1'b0), .out(multiplexer_10_out), .sel(B[1]));
  Multiplexer multiplexer_11 (.in0(multiplexer_3_out), .in1(multiplexer_1_out), .out(multiplexer_11_out), .sel(B[1]));
  Multiplexer multiplexer_12 (.in0(multiplexer_4_out), .in1(multiplexer_2_out), .out(multiplexer_12_out), .sel(B[1]));
  Multiplexer multiplexer_13 (.in0(multiplexer_5_out), .in1(multiplexer_3_out), .out(multiplexer_13_out), .sel(B[1]));
  Multiplexer multiplexer_14 (.in0(multiplexer_6_out), .in1(multiplexer_4_out), .out(multiplexer_14_out), .sel(B[1]));
  Multiplexer multiplexer_15 (.in0(multiplexer_7_out), .in1(multiplexer_5_out), .out(multiplexer_15_out), .sel(B[1]));
  Multiplexer multiplexer_16 (.in0(multiplexer_8_out), .in1(multiplexer_6_out), .out(multiplexer_16_out), .sel(B[1]));
  Multiplexer multiplexer_17 (.in0(multiplexer_9_out), .in1(1'b0), .out(multiplexer_17_out), .sel(B[2]));
  Multiplexer multiplexer_18 (.in0(multiplexer_10_out), .in1(1'b0), .out(multiplexer_18_out), .sel(B[2]));
  Multiplexer multiplexer_19 (.in0(multiplexer_11_out), .in1(1'b0), .out(multiplexer_19_out), .sel(B[2]));
  Multiplexer multiplexer_20 (.in0(multiplexer_12_out), .in1(1'b0), .out(multiplexer_20_out), .sel(B[2]));
  Multiplexer multiplexer_21 (.in0(multiplexer_13_out), .in1(multiplexer_9_out), .out(multiplexer_21_out), .sel(B[2]));
  Multiplexer multiplexer_22 (.in0(multiplexer_14_out), .in1(multiplexer_10_out), .out(multiplexer_22_out), .sel(B[2]));
  Multiplexer multiplexer_23 (.in0(multiplexer_15_out), .in1(multiplexer_11_out), .out(multiplexer_23_out), .sel(B[2]));
  Multiplexer multiplexer_24 (.in0(multiplexer_16_out), .in1(multiplexer_12_out), .out(multiplexer_24_out), .sel(B[2]));
  Multiplexer multiplexer_25 (.in0(multiplexer_17_out), .in1(1'b0), .out(R[0]), .sel(or_1_out));
  Multiplexer multiplexer_26 (.in0(multiplexer_18_out), .in1(1'b0), .out(R[1]), .sel(or_1_out));
  Multiplexer multiplexer_27 (.in0(multiplexer_19_out), .in1(1'b0), .out(R[2]), .sel(or_1_out));
  Multiplexer multiplexer_28 (.in0(multiplexer_20_out), .in1(1'b0), .out(R[3]), .sel(or_1_out));
  Multiplexer multiplexer_29 (.in0(multiplexer_21_out), .in1(1'b0), .out(R[4]), .sel(or_1_out));
  Multiplexer multiplexer_30 (.in0(multiplexer_22_out), .in1(1'b0), .out(R[5]), .sel(or_1_out));
  Multiplexer multiplexer_31 (.in0(multiplexer_23_out), .in1(1'b0), .out(R[6]), .sel(or_1_out));
  Multiplexer multiplexer_32 (.in0(multiplexer_24_out), .in1(1'b0), .out(R[7]), .sel(or_1_out));
  or or_1 (or_1_out, B[7], B[6], B[5], B[4], B[3]);

  // Other names for the same wires on the sheet: s0 = R[0]; s1 = R[1]; s2 = R[2]; s3 = R[3]; s4 = R[4]; s5 = R[5];
  //   s6 = R[6]; s7 = R[7]
endmodule

module srr (
  input  [7:0] A,
  input  [7:0] B,
  output [7:0] R
);

  wire multiplexer_1_out, multiplexer_2_out, multiplexer_3_out, multiplexer_4_out, multiplexer_5_out,
       multiplexer_6_out, multiplexer_7_out, multiplexer_8_out, multiplexer_9_out, multiplexer_10_out,
       multiplexer_11_out, multiplexer_12_out, multiplexer_13_out, multiplexer_14_out, multiplexer_15_out,
       multiplexer_16_out, multiplexer_17_out, multiplexer_18_out, multiplexer_19_out, multiplexer_20_out,
       multiplexer_21_out, multiplexer_22_out, multiplexer_23_out, multiplexer_24_out, or_1_out;

  Multiplexer multiplexer_1 (.in0(A[0]), .in1(A[1]), .out(multiplexer_1_out), .sel(B[0]));
  Multiplexer multiplexer_2 (.in0(A[1]), .in1(A[2]), .out(multiplexer_2_out), .sel(B[0]));
  Multiplexer multiplexer_3 (.in0(A[2]), .in1(A[3]), .out(multiplexer_3_out), .sel(B[0]));
  Multiplexer multiplexer_4 (.in0(A[3]), .in1(A[4]), .out(multiplexer_4_out), .sel(B[0]));
  Multiplexer multiplexer_5 (.in0(A[4]), .in1(A[5]), .out(multiplexer_5_out), .sel(B[0]));
  Multiplexer multiplexer_6 (.in0(A[5]), .in1(A[6]), .out(multiplexer_6_out), .sel(B[0]));
  Multiplexer multiplexer_7 (.in0(A[6]), .in1(A[7]), .out(multiplexer_7_out), .sel(B[0]));
  Multiplexer multiplexer_8 (.in0(A[7]), .in1(1'b0), .out(multiplexer_8_out), .sel(B[0]));
  Multiplexer multiplexer_9 (.in0(multiplexer_1_out), .in1(multiplexer_3_out), .out(multiplexer_9_out), .sel(B[1]));
  Multiplexer multiplexer_10 (.in0(multiplexer_2_out), .in1(multiplexer_4_out), .out(multiplexer_10_out), .sel(B[1]));
  Multiplexer multiplexer_11 (.in0(multiplexer_3_out), .in1(multiplexer_5_out), .out(multiplexer_11_out), .sel(B[1]));
  Multiplexer multiplexer_12 (.in0(multiplexer_4_out), .in1(multiplexer_6_out), .out(multiplexer_12_out), .sel(B[1]));
  Multiplexer multiplexer_13 (.in0(multiplexer_5_out), .in1(multiplexer_7_out), .out(multiplexer_13_out), .sel(B[1]));
  Multiplexer multiplexer_14 (.in0(multiplexer_6_out), .in1(multiplexer_8_out), .out(multiplexer_14_out), .sel(B[1]));
  Multiplexer multiplexer_15 (.in0(multiplexer_7_out), .in1(1'b0), .out(multiplexer_15_out), .sel(B[1]));
  Multiplexer multiplexer_16 (.in0(multiplexer_8_out), .in1(1'b0), .out(multiplexer_16_out), .sel(B[1]));
  Multiplexer multiplexer_17 (.in0(multiplexer_9_out), .in1(multiplexer_13_out), .out(multiplexer_17_out), .sel(B[2]));
  Multiplexer multiplexer_18 (.in0(multiplexer_10_out), .in1(multiplexer_14_out), .out(multiplexer_18_out), .sel(B[2]));
  Multiplexer multiplexer_19 (.in0(multiplexer_11_out), .in1(multiplexer_15_out), .out(multiplexer_19_out), .sel(B[2]));
  Multiplexer multiplexer_20 (.in0(multiplexer_12_out), .in1(multiplexer_16_out), .out(multiplexer_20_out), .sel(B[2]));
  Multiplexer multiplexer_21 (.in0(multiplexer_13_out), .in1(1'b0), .out(multiplexer_21_out), .sel(B[2]));
  Multiplexer multiplexer_22 (.in0(multiplexer_14_out), .in1(1'b0), .out(multiplexer_22_out), .sel(B[2]));
  Multiplexer multiplexer_23 (.in0(multiplexer_15_out), .in1(1'b0), .out(multiplexer_23_out), .sel(B[2]));
  Multiplexer multiplexer_24 (.in0(multiplexer_16_out), .in1(1'b0), .out(multiplexer_24_out), .sel(B[2]));
  Multiplexer multiplexer_25 (.in0(multiplexer_17_out), .in1(1'b0), .out(R[0]), .sel(or_1_out));
  Multiplexer multiplexer_26 (.in0(multiplexer_18_out), .in1(1'b0), .out(R[1]), .sel(or_1_out));
  Multiplexer multiplexer_27 (.in0(multiplexer_19_out), .in1(1'b0), .out(R[2]), .sel(or_1_out));
  Multiplexer multiplexer_28 (.in0(multiplexer_20_out), .in1(1'b0), .out(R[3]), .sel(or_1_out));
  Multiplexer multiplexer_29 (.in0(multiplexer_21_out), .in1(1'b0), .out(R[4]), .sel(or_1_out));
  Multiplexer multiplexer_30 (.in0(multiplexer_22_out), .in1(1'b0), .out(R[5]), .sel(or_1_out));
  Multiplexer multiplexer_31 (.in0(multiplexer_23_out), .in1(1'b0), .out(R[6]), .sel(or_1_out));
  Multiplexer multiplexer_32 (.in0(multiplexer_24_out), .in1(1'b0), .out(R[7]), .sel(or_1_out));
  or or_1 (or_1_out, B[7], B[6], B[5], B[4], B[3]);

  // Other names for the same wires on the sheet: s0 = R[0]; s1 = R[1]; s2 = R[2]; s3 = R[3]; s4 = R[4]; s5 = R[5];
  //   s6 = R[6]; s7 = R[7]
endmodule

module movhighmovlow (
  input  [7:0] A,
  input  [3:0] imm,
  input  Seletor,
  output [7:0] R
);

  Multiplexer #(.width(8)) multiplexer_1 (.in0({imm, A[3:0]}), .in1({A[7:4], imm}), .out(R), .sel(Seletor));

  // Notes on the sheet:
  //   High
  //   Low
endmodule

module compbrz (
  input  [7:0] A,
  output brzr
);

  Comparator comparator_1 (.a(A), .b({8{1'b0}}), .eq(brzr));  // open: gt, lt
endmodule

module lookupulaop (
  input  [3:0] Opcode,
  output [2:0] Ulaop
);

  ROM #(.addrWidth(4), .dataWidth(3)) rom_1 (.addr(Opcode), .data(Ulaop));

  // Notes on the sheet:
  //   contents of rom_1 (hex, n*v repeats v):
  //   8*7 0 1 6 2 3 4 5 2
endmodule
